# Fritzing sketch RFID_Schema (saved by Fritzing 0.9.3b)

parts:
  Componente1 = RFID-RC522-v2
  Arduino_RFID = Arduino Uno (Rev3)

nets:
  N1: Componente1.SDA, Arduino_RFID.D10_PWM/SS
  N2: Componente1.SCK, Arduino_RFID.D13/SCK
  N3: Componente1.MOSI, Arduino_RFID.D11_PWM/MOSI
  N4: Componente1.MISO, Arduino_RFID.D12/MISO
  GND: Componente1.GND, Arduino_RFID.GND
  N5: Componente1.RST, Arduino_RFID.D9_PWM
  3.3V: Componente1.3.3V, Arduino_RFID.3V3

notes:
  3.3 V
  Modulo Pins
  SDA 10
  SCK 13
  MOSI 11
  MISO 12
  IRQ -
  RST 9

custom parts:
  RFID-RC522-v2: A simple China made RFID-RC522 Reader; do check the pin labels, as this is a MFRC522 based clone.

// code stored in the sketch: RFID.ino
#include <SPI.h>
#include <MFRC522.h>

#define RST_PIN  9    //Pin 9 para el reset del RC522
#define SS_PIN  10   //Pin 10 para el SS (SDA) del RC522
MFRC522 mfrc522(SS_PIN, RST_PIN); //Creamos el objeto para el RC522

void setup() {
  Serial.begin(9600); //Iniciamos la comunicación  serial
  SPI.begin();        //Iniciamos el Bus SPI
  mfrc522.PCD_Init(); // Iniciamos  el MFRC522
  Serial.println("Lectura del UID");
}

void loop() {
  // Revisamos si hay nuevas tarjetas  presentes
  if ( mfrc522.PICC_IsNewCardPresent()) 
        {  
      //Seleccionamos una tarjeta
            if ( mfrc522.PICC_ReadCardSerial()) 
            {
                  // Enviamos serialemente su UID
                  Serial.print("Card UID:");
                  for (byte i = 0; i < mfrc522.uid.size; i++) {
                          Serial.print(mfrc522.uid.uidByte[i] < 0x10 ? " 0" : " ");
                          Serial.print(mfrc522.uid.uidByte[i], HEX);   
                  } 
                  Serial.println();
                  // Terminamos la lectura de la tarjeta  actual
                  mfrc522.PICC_HaltA();         
            }      
  } 
}
